# Fritzing sketch leds (saved by Fritzing 0.8.5b)
stripboards: 1

parts:
  LED1 = LED - 5mm [color="Red (633nm)" package="5 mm [THT]"]
  LED2 = LED - 5mm [color="Red (633nm)" package="5 mm [THT]"]
  LED4 = LED - 5mm [color="Red (633nm)" package="5 mm [THT]"]
  LED6 = LED - 5mm [color="Red (633nm)" package="5 mm [THT]"]
  LED3 = LED - 5mm [color="Red (633nm)" package="5 mm [THT]"]
  LED7 = LED - 5mm [color="Red (633nm)" package="5 mm [THT]"]
  LED5 = LED - 5mm [color="Red (633nm)" package="5 mm [THT]"]
  J1 = shrouded pin header, 10 pins [form="♂ (shrouded male)"]

nets (from the schematic view):
  N1: LED1.cathode, J1.pin2
  N2: LED1.anode, LED2.anode, LED4.anode, LED6.anode, LED3.anode, LED7.anode, LED5.anode, J1.pin1
  N3: LED2.cathode, J1.pin10
  N4: LED4.cathode, J1.pin8
  N5: LED6.cathode, J1.pin4
  N6: LED3.cathode, J1.pin9
  N7: LED7.cathode, J1.pin3
  N8: LED5.cathode, J1.pin7
