# Fritzing sketch shield (saved by Fritzing 0.8.5b)

parts:
  Part1 = Arduino Prototyping Shield
  R18 = Resistor [tolerance=±5% resistance=10 package=THT]
  Part3 = Triple Axis Accelerometer Breakout - ADXL345
  J1 = male pin header, 8 pins [form="♂ (male)"]
  IC1 = IC, DIP package, 18 pins [chip_label="ULN 2803A"]
  J2 = male pin header, 8 pins [form="♂ (male)"]
  J3 = male pin header, 8 pins [form="♂ (male)"]
  J4 = male pin header, 8 pins [form="♂ (male)"]
  J5 = male pin header, 8 pins [form="♂ (male)"]
  J6 = male pin header, 8 pins [form="♂ (male)"]
  IC2 = IC, DIP package, 18 pins [chip_label="UDN 2981"]
  R19 = Resistor [tolerance=±5% resistance=10 package=THT]
  R20 = Resistor [tolerance=±5% resistance=10 package=THT]
  R21 = Resistor [tolerance=±5% resistance=10 package=THT]
  R22 = Resistor [tolerance=±5% resistance=10 package=THT]
  R23 = Resistor [tolerance=±5% resistance=10 package=THT]
  VCC1 = Battery block 9V
  J7 = male pin header, 2 pins [form="♂ (male)"]
  Part4 = Pegelwandler (4-Kanal)

nets:
  N1: Part1.+5V, Part1.N$238, Part1.N$249, Part1.N$332, IC1.pin10, IC2.pin9, Part4.HV_1, Part4.HV_2
  GND: Part1.GND, Part1.N$118, Part1.N$201, Part1.N$335, Part3.GND, IC1.pin9, IC2.pin10, VCC1.-, J7.pin1
  N2: Part1.+9V, VCC1.+, J7.pin2
  N3: Part1.D10, Part1.N$235, Part4.1_HV_1
  N4: Part1.D8, Part1.N$434, IC1.pin7
  N5: Part1.D11, Part1.N$228, Part4.2_HV_2
  N6: Part1.D12, Part1.N$232, Part4.2_HV_1
  N7: Part1.D13, Part1.N$245, Part4.1_HV_2
  N8: Part1.D2, Part1.N$428, IC1.pin1
  N9: Part1.D3, Part1.N$429, IC1.pin2
  N10: Part1.D4, Part1.N$431, IC1.pin3
  N11: Part1.D5, Part1.N$430, IC1.pin4
  N12: Part1.D6, Part1.N$432, IC1.pin5
  N13: Part1.D7, Part1.N$433, IC1.pin6
  N14: Part1.A0, Part1.N$55, IC2.pin6
  N15: Part1.A1, Part1.N$65, IC2.pin5
  N16: Part1.A2, Part1.N$79, IC2.pin4
  N17: Part1.A3, Part1.N$84, IC2.pin3
  N18: Part1.A4, Part1.N$87, IC2.pin2
  N19: Part1.A5, Part1.N$67, IC2.pin1
  3.3V: Part1.3.3V, Part1.N$63, Part1.N$123, Part1.N$132, Part3.VCC, Part4.LV_2, Part4.LV_1
  N20: Part1.N$17, Part1.N$57, Part1.N$356, Part1.N$371, Part1.N$378, Part1.N$381, Part1.N$410, J1.pin6, IC1.pin16, J2.pin6, J3.pin6, J4.pin6, J5.pin6, J6.pin6
  N21: Part1.N$27, IC2.pin11
  N22: Part1.N$34, IC2.pin8
  N23: Part1.N$37, IC2.pin12
  N24: Part1.N$41, IC2.pin7
  N25: Part1.N$45, Part1.N$296, Part1.N$297, Part1.N$313, Part1.N$316, Part1.N$364, Part1.N$374, J1.pin3, IC1.pin13, J2.pin3, J3.pin3, J4.pin3, J5.pin3, J6.pin3
  N26: Part1.N$48, IC2.pin13, R23.Pin_0
  N27: Part1.N$52, Part1.N$320, Part1.N$355, Part1.N$366, Part1.N$370, Part1.N$379, Part1.N$408, J1.pin7, IC1.pin17, J2.pin7, J3.pin7, J4.pin7, J5.pin7, J6.pin7
  N28: Part1.N$62, IC2.pin14, R22.Pin_0
  N29: Part1.N$64, Part1.N$135, Part3.CS, Part4.1_LV_1
  N30: Part1.N$69, Part1.N$294, Part1.N$295, Part1.N$298, Part1.N$312, Part1.N$361, Part1.N$362, J1.pin2, IC1.pin12, J2.pin2, J3.pin2, J4.pin2, J5.pin2, J6.pin2
  N31: Part1.N$72, IC2.pin15, R21.Pin_0
  N32: Part1.N$76, R18.Pin_0, IC2.pin18
  N33: Part1.N$77, IC2.pin17, R19.Pin_0
  N34: Part1.N$81, Part1.N$327, Part1.N$354, Part1.N$369, Part1.N$380, Part1.N$383, Part1.N$402, J1.pin8, IC1.pin18, J2.pin8, J3.pin8, J4.pin8, J5.pin8, J6.pin8
  N35: Part1.N$86, IC2.pin16, R20.Pin_0
  N36: Part1.N$88, Part3.INT1
  N37: Part1.N$89, Part3.INT2
  N38: Part1.N$91, Part1.N$156, Part3.SDO, Part4.2_LV_1
  N39: Part1.N$96, Part1.N$180, Part3.SDA, Part4.2_LV_2
  N40: Part1.N$108, Part1.N$192, Part3.SCL, Part4.1_LV_2
  N41: Part1.N$165, Part1.N$318, Part1.N$319, Part1.N$357, Part1.N$367, Part1.N$372, Part1.N$377, J1.pin5, IC1.pin15, J2.pin5, J3.pin5, J4.pin5, J5.pin5, J6.pin5
  N42: Part1.N$241, IC1.pin11
  N43: Part1.N$262, Part1.N$263, R18.Pin_1, J1.pin1
  N44: Part1.N$276, Part1.N$293, J3.pin1, R20.Pin_1
  N45: Part1.N$281, Part1.N$282, J2.pin1, R19.Pin_1
  N46: Part1.N$283, Part1.N$375, J4.pin1, R21.Pin_1
  N47: Part1.N$292, Part1.N$363, J5.pin1, R22.Pin_1
  N48: Part1.N$299, Part1.N$317, Part1.N$358, Part1.N$365, Part1.N$373, Part1.N$376, Part1.N$411, J1.pin4, IC1.pin14, J2.pin4, J3.pin4, J4.pin4, J5.pin4, J6.pin4
  N49: Part1.N$359, Part1.N$360, J6.pin1, R23.Pin_1
  N50: Part1.N$435, IC1.pin8

custom parts:
  Pegelwandler (4-Kanal): Pegelwandler Baustein mit 4 Ein- / Ausgängen. Mit diesem Wandler kann man die Pegel von zwei unterschiedlichen Signalebenen mit einander verbinden. z.B. 5V System mit 3,3V. Der Wandler arbeitet aber auch mit 1,8V und/oder 2,8V Pegeln und kann für I2C verwendet werden. Der Wandler braucht zum Betrieb die beiden Versorgungsspannungen, diese werden an hohe Versorgungsspannung an den "HV" Pin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
